# Fritzing sketch ThermoHome_pi (saved by Fritzing 0.9.4)
breadboards: 1

parts:
  DHT22 = Humidity and Temperature Sensor RHT03
  R1 = Resistor [tolerance=±5% resistance=220 package=THT]
  Raspberry_Pi_1 = Raspberry Pi 3 [part_number=RPI-3-V1.2]
  SONGLE_SRD-05VDC-SL-C = Keyes Relay [package=THT]

nets:
  VCC: DHT22.Vcc, R1.Pin_1, Raspberry_Pi_1.5V
  N1: DHT22.Data-signal, R1.Pin_0, Raspberry_Pi_1.GPIO4
  N2: DHT22.GND_2, Raspberry_Pi_1.GND
  3V3: Raspberry_Pi_1.3v3, SONGLE_SRD-05VDC-SL-C.VCC
  N3: Raspberry_Pi_1.GPIO17, SONGLE_SRD-05VDC-SL-C.ground

custom parts:
  Keyes Relay: The Keyes 5V relay module is suitable for SCM development, home appliance control. It uses a 5V~12V TIL control signal which can control DC / AC signal.
